# Fritzing sketch sketch (saved by Fritzing 0.9.6b)
breadboards: 1

parts:
  Mod1 = Raspberry Pi Pico W
  J2 = RJ11 Jack [package=rj11-6]

nets:
  N1: Mod1.pin_1, Mod1.pin_6, Mod1.pin_7, J2.B, J2.G
  N2: Mod1.pin_3, Mod1.pin_8, Mod1.pin_13, Mod1.pin_18, Mod1.pin_23, Mod1.pin_28, Mod1.pin_33, Mod1.pin_38, J2.R
  N3: Mod1.pin_36, J2.Y

notes:
  white - TX
  yellow - RX
  black - GRD
  red - VCC
  Y - VCC
  B - RX
  G - TX
  R - GND

custom parts:
  Raspberry Pi Pico W: Raspberry Pi Pico W. Based around the RP2040 microcontroller the Pico W is a low cost microcontroller device bringing Raspberry Pi quality, cost, and easy of use to the microcontroller space. The areas marked KEEPOUT in pcb silkscreen should not have traces running through them to avoid shorts on a soldered in module!
  RJ11 Jack: RJ11 Jack Simple 6 pin RJ11 jack. Commonly found on CAT3 devices and Microchip programmers. SKU: PRT-00132
